# Fritzing sketch Untitled Sketch 3 (saved by Fritzing 0.9.3b)

parts:
  U1 = ESP32S-HiLetgo [part_number=ESP32S-HiLetgo]
  HC-SR04_Sensor_1 = HC-SR04 Ultrasonic Distance Sensor
  DFRobot_DFPlayer_Mini1 = DFRobot DFPlayer Mini [part_number=DFR0299]
  SPKR1 = Loudspeaker
  amplifier_board = Mono 2.6W Class D Amplifier [package=8-tdfn-ep]
  U5 = LIPO-110mAh [package=lipo-110]
  R1 = Photocell (LDR) [package=THT]
  R2 = Resistor [tolerance=±5% resistance=10k package="1206 [SMD]"]

nets:
  N1: U1.GPIO25, HC-SR04_Sensor_1.GND
  N2: U1.GPIO26, HC-SR04_Sensor_1.TRIG
  VIN: U1.VIN, amplifier_board.VDD, U5.+, R1.pin_1
  N3: U1.GPIO15, R1.pin_0, R2.Pin_1
  N4: U1.GPIO16, DFRobot_DFPlayer_Mini1.TX
  N5: U1.GPIO17, DFRobot_DFPlayer_Mini1.RX
  GND: U1.GND, HC-SR04_Sensor_1.ECHO, DFRobot_DFPlayer_Mini1.GND-1, DFRobot_DFPlayer_Mini1.GND-2, amplifier_board.GND, U5.-, R2.Pin_0
  VCC: HC-SR04_Sensor_1.VCC, DFRobot_DFPlayer_Mini1.VCC
  N6: DFRobot_DFPlayer_Mini1.SPK_1, amplifier_board.IN+
  N7: DFRobot_DFPlayer_Mini1.SPK_2, amplifier_board.IN-
  N8: SPKR1.pin1, amplifier_board.OUT+
  N9: SPKR1.pin2, amplifier_board.OUT-

custom parts:
  ESP32S-HiLetgo: HiLetgo ESP-WROOM-32 ESP32 ESP-32S Development Board 2.4GHz Dual-Mode WiFi + Bluetooth Dual Cores Microcontroller The ESP32 integrated with Antenna switches, RF Balun, power amplifiers, low-noise amplifiers, filters, and management modules, and the entire solution occupies the least area of PCB. 2.4 GHz Wi-Fi plus Bluetooth dual-mode chip, with TSMC Ultra-low power consumption 40nm technology,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
